// Logisim project control-logic.circ as structural Verilog: 1 circuit, main circuit control_logic
module control_logic (
  input  [31:0] Instruction,
  input  BrEq,
  input  BrLt,
  output PCSel,
  output RegWEn,
  output [2:0] ImmSel,
  output BrUn,
  output ASel,
  output BSel,
  output [3:0] ALUSel,
  output MemRW,
  output [1:0] WBSel
);

  wire and_1_out, comparator_1_eq, comparator_2_eq, comparator_3_eq, comparator_4_eq, comparator_5_eq,
       comparator_6_eq, comparator_7_eq, comparator_8_eq, comparator_9_eq, comparator_10_eq,
       comparator_11_eq, comparator_12_eq, comparator_13_eq, comparator_14_eq, comparator_15_eq,
       comparator_16_eq, comparator_17_eq, comparator_18_eq, comparator_19_eq, comparator_20_eq,
       comparator_21_eq, comparator_22_eq, comparator_23_eq, comparator_24_eq, comparator_25_eq,
       comparator_26_eq, comparator_27_eq, comparator_28_eq, comparator_29_eq, comparator_30_eq,
       comparator_31_eq, comparator_32_eq, comparator_33_eq, comparator_34_eq, comparator_35_eq,
       comparator_36_eq, comparator_37_eq, comparator_38_eq, comparator_39_eq, comparator_40_eq,
       comparator_41_eq, comparator_42_eq, comparator_43_eq, comparator_44_eq, comparator_45_eq,
       comparator_46_eq, comparator_47_eq, comparator_48_eq, comparator_49_eq, comparator_50_eq,
       comparator_51_eq, comparator_52_eq, comparator_53_eq, comparator_54_eq, comparator_55_eq,
       comparator_56_eq, comparator_57_eq, comparator_58_eq, comparator_59_eq, comparator_60_eq,
       comparator_61_eq, comparator_62_eq, comparator_63_eq, comparator_64_eq, multiplexer_1_out,
       multiplexer_2_out, multiplexer_3_out, multiplexer_12_out, multiplexer_13_out, multiplexer_14_out,
       multiplexer_15_out, multiplexer_16_out, multiplexer_17_out, multiplexer_18_out, multiplexer_19_out,
       multiplexer_20_out, multiplexer_21_out, multiplexer_22_out, multiplexer_23_out, multiplexer_24_out,
       multiplexer_25_out, multiplexer_26_out, multiplexer_27_out, multiplexer_29_out, multiplexer_30_out,
       multiplexer_31_out, multiplexer_32_out, multiplexer_33_out, multiplexer_34_out, multiplexer_35_out,
       multiplexer_36_out, multiplexer_37_out, multiplexer_38_out, multiplexer_39_out, multiplexer_40_out,
       multiplexer_41_out, not_1_out, not_2_out, not_3_out, not_4_out;
  wire [1:0] multiplexer_62_out, multiplexer_63_out, multiplexer_64_out, or_7_out;
  wire [2:0] multiplexer_4_out, multiplexer_5_out, multiplexer_6_out, multiplexer_7_out, multiplexer_8_out,
       multiplexer_9_out, multiplexer_10_out, multiplexer_11_out;
  wire [3:0] multiplexer_42_out, multiplexer_43_out, multiplexer_44_out, multiplexer_45_out,
       multiplexer_46_out, multiplexer_47_out, multiplexer_48_out, multiplexer_49_out, multiplexer_50_out,
       multiplexer_51_out, multiplexer_52_out, multiplexer_53_out, multiplexer_54_out, multiplexer_55_out,
       multiplexer_56_out, multiplexer_57_out, multiplexer_58_out, multiplexer_59_out, multiplexer_60_out,
       multiplexer_61_out;
  wire [15:0] rom_1_data;

  Comparator #(.width(7)) comparator_1 (.a(7'b1100011), .b(Instruction[6:0]), .eq(comparator_1_eq));  // open: gt, lt
  Comparator #(.width(3)) comparator_2 (.a(Instruction[14:12]), .b(3'b000), .eq(comparator_2_eq));  // open: gt, lt
  Comparator #(.width(7)) comparator_3 (.a(7'b0010011), .b(Instruction[6:0]), .eq(comparator_3_eq));  // open: gt, lt
  Comparator #(.width(7)) comparator_4 (.a(7'b1100011), .b(Instruction[6:0]), .eq(comparator_4_eq));  // open: gt, lt
  Comparator #(.width(7)) comparator_5 (.a(7'b0000011), .b(Instruction[6:0]), .eq(comparator_5_eq));  // open: gt, lt
  Comparator #(.width(7)) comparator_6 (.a(7'b0100011), .b(Instruction[6:0]), .eq(comparator_6_eq));  // open: gt, lt
  Comparator #(.width(7)) comparator_7 (.a(7'b0110111), .b(Instruction[6:0]), .eq(comparator_7_eq));  // open: gt, lt
  Comparator #(.width(7)) comparator_8 (.a(7'b0010111), .b(Instruction[6:0]), .eq(comparator_8_eq));  // open: gt, lt
  Comparator #(.width(7)) comparator_9 (.a(7'b1101111), .b(Instruction[6:0]), .eq(comparator_9_eq));  // open: gt, lt
  Comparator #(.width(7)) comparator_10 (.a(7'b1100111), .b(Instruction[6:0]), .eq(comparator_10_eq));  // open: gt, lt
  Comparator #(.width(3)) comparator_11 (.a(Instruction[14:12]), .b(3'b101), .eq(comparator_11_eq));  // open: gt, lt
  Multiplexer multiplexer_1 (.in0(1'b0), .in1(BrEq), .out(multiplexer_1_out), .sel(comparator_2_eq));
  not not_1 (not_1_out, BrLt);
  Comparator #(.width(7)) comparator_12 (.a(7'b1101111), .b(Instruction[6:0]), .eq(comparator_12_eq));  // open: gt, lt
  Multiplexer multiplexer_2 (.in0(1'b0), .in1(1'b1), .out(multiplexer_2_out), .sel(comparator_12_eq));
  Comparator #(.width(7)) comparator_13 (.a(7'b1100111), .b(Instruction[6:0]), .eq(comparator_13_eq));  // open: gt, lt
  Multiplexer multiplexer_3 (.in0(1'b0), .in1(1'b1), .out(multiplexer_3_out), .sel(comparator_13_eq));
  Multiplexer #(.width(3)) multiplexer_4 (.in0(3'b000), .in1(3'b000), .out(multiplexer_4_out), .sel(comparator_3_eq));
  Multiplexer #(.width(3)) multiplexer_5 (.in0(3'b000), .in1(3'b010), .out(multiplexer_5_out), .sel(comparator_4_eq));
  Multiplexer #(.width(3)) multiplexer_6 (.in0(3'b000), .in1(3'b000), .out(multiplexer_6_out), .sel(comparator_5_eq));
  Multiplexer #(.width(3)) multiplexer_7 (.in0(3'b000), .in1(3'b001), .out(multiplexer_7_out), .sel(comparator_6_eq));
  Multiplexer #(.width(3)) multiplexer_8 (.in0(3'b000), .in1(3'b011), .out(multiplexer_8_out), .sel(comparator_7_eq));
  Multiplexer #(.width(3)) multiplexer_9 (.in0(3'b000), .in1(3'b011), .out(multiplexer_9_out), .sel(comparator_8_eq));
  Multiplexer #(.width(3)) multiplexer_10 (.in0(3'b000), .in1(3'b100), .out(multiplexer_10_out), .sel(comparator_9_eq));
  Multiplexer #(.width(3)) multiplexer_11 (
    .in0(3'b000), .in1(3'b000), .out(multiplexer_11_out), .sel(comparator_10_eq));
  Comparator #(.width(7)) comparator_14 (.a(7'b0010011), .b(Instruction[6:0]), .eq(comparator_14_eq));  // open: gt, lt
  Multiplexer multiplexer_12 (.in0(1'b0), .in1(1'b1), .out(multiplexer_12_out), .sel(comparator_14_eq));
  Comparator #(.width(7)) comparator_15 (.a(7'b0110011), .b(Instruction[6:0]), .eq(comparator_15_eq));  // open: gt, lt
  Multiplexer multiplexer_13 (.in0(1'b0), .in1(1'b1), .out(multiplexer_13_out), .sel(comparator_15_eq));
  Comparator #(.width(7)) comparator_16 (.a(7'b1100011), .b(Instruction[6:0]), .eq(comparator_16_eq));  // open: gt, lt
  Multiplexer multiplexer_14 (.in0(1'b0), .in1(1'b0), .out(multiplexer_14_out), .sel(comparator_16_eq));
  Comparator #(.width(7)) comparator_17 (.a(7'b0000011), .b(Instruction[6:0]), .eq(comparator_17_eq));  // open: gt, lt
  Multiplexer multiplexer_15 (.in0(1'b0), .in1(1'b1), .out(multiplexer_15_out), .sel(comparator_17_eq));
  Comparator #(.width(7)) comparator_18 (.a(7'b0100011), .b(Instruction[6:0]), .eq(comparator_18_eq));  // open: gt, lt
  Multiplexer multiplexer_16 (.in0(1'b0), .in1(1'b0), .out(multiplexer_16_out), .sel(comparator_18_eq));
  Comparator #(.width(7)) comparator_19 (.a(7'b0110111), .b(Instruction[6:0]), .eq(comparator_19_eq));  // open: gt, lt
  Multiplexer multiplexer_17 (.in0(1'b0), .in1(1'b1), .out(multiplexer_17_out), .sel(comparator_19_eq));
  Comparator #(.width(7)) comparator_20 (.a(7'b0010111), .b(Instruction[6:0]), .eq(comparator_20_eq));  // open: gt, lt
  Multiplexer multiplexer_18 (.in0(1'b0), .in1(1'b1), .out(multiplexer_18_out), .sel(comparator_20_eq));
  Comparator #(.width(7)) comparator_21 (.a(7'b1101111), .b(Instruction[6:0]), .eq(comparator_21_eq));  // open: gt, lt
  Multiplexer multiplexer_19 (.in0(1'b0), .in1(1'b1), .out(multiplexer_19_out), .sel(comparator_21_eq));
  Comparator #(.width(7)) comparator_22 (.a(7'b1100111), .b(Instruction[6:0]), .eq(comparator_22_eq));  // open: gt, lt
  Multiplexer multiplexer_20 (.in0(1'b0), .in1(1'b1), .out(multiplexer_20_out), .sel(comparator_22_eq));
  Comparator #(.width(7)) comparator_23 (.a(7'b1100011), .b(Instruction[6:0]), .eq(comparator_23_eq));  // open: gt, lt
  ROM #(.addrWidth(6), .dataWidth(16)) rom_1 (.data(rom_1_data));  // open: addr
  Comparator #(.width(3)) comparator_24 (.a(Instruction[14:12]), .b(3'b111), .eq(comparator_24_eq));  // open: gt, lt
  Multiplexer multiplexer_21 (
    .in0(multiplexer_1_out), .in1(not_1_out), .out(multiplexer_21_out), .sel(comparator_11_eq));
  not not_2 (not_2_out, BrLt);
  Comparator #(.width(3)) comparator_25 (.a(3'b111), .b(Instruction[14:12]), .eq(comparator_25_eq));  // open: gt, lt
  Multiplexer multiplexer_22 (.in0(1'b0), .in1(1'b1), .out(multiplexer_22_out), .sel(comparator_25_eq));
  Comparator #(.width(3)) comparator_26 (.a(Instruction[14:12]), .b(3'b100), .eq(comparator_26_eq));  // open: gt, lt
  Multiplexer multiplexer_23 (
    .in0(multiplexer_21_out), .in1(not_2_out), .out(multiplexer_23_out), .sel(comparator_24_eq));
  Multiplexer multiplexer_24 (.in0(multiplexer_23_out), .in1(BrLt), .out(multiplexer_24_out), .sel(comparator_26_eq));
  assign ImmSel = multiplexer_4_out | multiplexer_5_out | multiplexer_6_out | multiplexer_7_out | multiplexer_8_out | multiplexer_9_out | multiplexer_10_out | multiplexer_11_out;  // OR_Gate or_1, 3 bits wide
  Comparator #(.width(3)) comparator_27 (.a(3'b110), .b(Instruction[14:12]), .eq(comparator_27_eq));  // open: gt, lt
  Comparator #(.width(3)) comparator_28 (.a(Instruction[14:12]), .b(3'b110), .eq(comparator_28_eq));  // open: gt, lt
  Multiplexer multiplexer_25 (.in0(multiplexer_24_out), .in1(BrLt), .out(multiplexer_25_out), .sel(comparator_28_eq));
  or or_2 (PCSel, multiplexer_29_out, multiplexer_2_out, multiplexer_3_out);
  or or_3 (RegWEn, multiplexer_12_out, multiplexer_13_out, multiplexer_14_out, multiplexer_15_out, multiplexer_16_out, multiplexer_17_out, multiplexer_18_out, multiplexer_19_out, multiplexer_20_out);
  Multiplexer multiplexer_26 (.in0(multiplexer_22_out), .in1(1'b1), .out(multiplexer_26_out), .sel(comparator_27_eq));
  Comparator #(.width(3)) comparator_29 (.a(Instruction[14:12]), .b(3'b001), .eq(comparator_29_eq));  // open: gt, lt
  Multiplexer multiplexer_27 (
    .in0(multiplexer_25_out), .in1(not_3_out), .out(multiplexer_27_out), .sel(comparator_29_eq));
  not not_3 (not_3_out, BrEq);
  Multiplexer multiplexer_28 (.in0(1'b0), .in1(multiplexer_26_out), .out(BrUn), .sel(comparator_23_eq));
  Multiplexer multiplexer_29 (.in0(1'b0), .in1(multiplexer_27_out), .out(multiplexer_29_out), .sel(comparator_1_eq));
  Comparator #(.width(7)) comparator_30 (.a(7'b0010011), .b(Instruction[6:0]), .eq(comparator_30_eq));  // open: gt, lt
  Comparator #(.width(7)) comparator_31 (.a(7'b0110011), .b(Instruction[6:0]), .eq(comparator_31_eq));  // open: gt, lt
  Comparator #(.width(7)) comparator_32 (.a(7'b1100011), .b(Instruction[6:0]), .eq(comparator_32_eq));  // open: gt, lt
  Comparator #(.width(7)) comparator_33 (.a(7'b0000011), .b(Instruction[6:0]), .eq(comparator_33_eq));  // open: gt, lt
  Comparator #(.width(7)) comparator_34 (.a(7'b0100011), .b(Instruction[6:0]), .eq(comparator_34_eq));  // open: gt, lt
  Comparator #(.width(7)) comparator_35 (.a(7'b0110111), .b(Instruction[6:0]), .eq(comparator_35_eq));  // open: gt, lt
  Comparator #(.width(7)) comparator_36 (.a(7'b0010111), .b(Instruction[6:0]), .eq(comparator_36_eq));  // open: gt, lt
  Comparator #(.width(7)) comparator_37 (.a(7'b1101111), .b(Instruction[6:0]), .eq(comparator_37_eq));  // open: gt, lt
  Comparator #(.width(7)) comparator_38 (.a(7'b1100111), .b(Instruction[6:0]), .eq(comparator_38_eq));  // open: gt, lt
  Comparator #(.width(7)) comparator_39 (.a({7{1'b0}}), .b(Instruction[31:25]), .eq(comparator_39_eq));  // open: gt, lt
  Comparator #(.width(7)) comparator_40 (.a(7'b1100011), .b(Instruction[6:0]), .eq(comparator_40_eq));  // open: gt, lt
  Multiplexer multiplexer_30 (.in0(1'b0), .in1(1'b1), .out(multiplexer_30_out), .sel(comparator_40_eq));
  Comparator #(.width(7)) comparator_41 (.a(7'b0010111), .b(Instruction[6:0]), .eq(comparator_41_eq));  // open: gt, lt
  Multiplexer multiplexer_31 (.in0(1'b0), .in1(1'b1), .out(multiplexer_31_out), .sel(comparator_41_eq));
  Comparator #(.width(7)) comparator_42 (.a(7'b1101111), .b(Instruction[6:0]), .eq(comparator_42_eq));  // open: gt, lt
  Multiplexer multiplexer_32 (.in0(1'b0), .in1(1'b1), .out(multiplexer_32_out), .sel(comparator_42_eq));
  Multiplexer multiplexer_33 (.in0(1'b0), .in1(1'b1), .out(multiplexer_33_out), .sel(comparator_30_eq));
  Multiplexer multiplexer_34 (.in0(1'b0), .in1(1'b0), .out(multiplexer_34_out), .sel(comparator_31_eq));
  Multiplexer multiplexer_35 (.in0(1'b0), .in1(1'b1), .out(multiplexer_35_out), .sel(comparator_32_eq));
  Multiplexer multiplexer_36 (.in0(1'b0), .in1(1'b1), .out(multiplexer_36_out), .sel(comparator_33_eq));
  Multiplexer multiplexer_37 (.in0(1'b0), .in1(1'b1), .out(multiplexer_37_out), .sel(comparator_34_eq));
  Multiplexer multiplexer_38 (.in0(1'b0), .in1(1'b1), .out(multiplexer_38_out), .sel(comparator_35_eq));
  Multiplexer multiplexer_39 (.in0(1'b0), .in1(1'b1), .out(multiplexer_39_out), .sel(comparator_36_eq));
  Multiplexer multiplexer_40 (.in0(1'b0), .in1(1'b1), .out(multiplexer_40_out), .sel(comparator_37_eq));
  Multiplexer multiplexer_41 (.in0(1'b0), .in1(1'b1), .out(multiplexer_41_out), .sel(comparator_38_eq));
  Comparator #(.width(7)) comparator_43 (.a(7'b0010011), .b(Instruction[6:0]), .eq(comparator_43_eq));  // open: gt, lt
  Multiplexer #(.width(4)) multiplexer_42 (
    .in0(4'b0000), .in1(4'b0101), .out(multiplexer_42_out), .sel(comparator_39_eq));
  Comparator #(.width(7)) comparator_44 (.a(7'b0110011), .b(Instruction[6:0]), .eq(comparator_44_eq));  // open: gt, lt
  Multiplexer #(.width(4)) multiplexer_43 (
    .in0(4'b0000), .in1(4'b0000), .out(multiplexer_43_out), .sel(comparator_45_eq));
  Comparator #(.width(7)) comparator_45 (.a({7{1'b0}}), .b(Instruction[31:25]), .eq(comparator_45_eq));  // open: gt, lt
  Multiplexer #(.width(4)) multiplexer_44 (
    .in0(4'b0000), .in1(4'b0001), .out(multiplexer_44_out), .sel(comparator_46_eq));
  Comparator #(.width(7)) comparator_46 (.a({7{1'b0}}), .b(Instruction[31:25]), .eq(comparator_46_eq));  // open: gt, lt
  Multiplexer #(.width(4)) multiplexer_45 (
    .in0(4'b0000), .in1(4'b0101), .out(multiplexer_45_out), .sel(comparator_47_eq));
  Comparator #(.width(7)) comparator_47 (.a({7{1'b0}}), .b(Instruction[31:25]), .eq(comparator_47_eq));  // open: gt, lt
  Comparator #(.width(7)) comparator_48 (.a(7'b1100011), .b(Instruction[6:0]), .eq(comparator_48_eq));  // open: gt, lt
  Multiplexer #(.width(4)) multiplexer_46 (
    .in0(4'b0000), .in1(4'b0000), .out(multiplexer_46_out), .sel(comparator_48_eq));
  Comparator #(.width(7)) comparator_49 (.a(7'b0000011), .b(Instruction[6:0]), .eq(comparator_49_eq));  // open: gt, lt
  Multiplexer #(.width(4)) multiplexer_47 (
    .in0(4'b0000), .in1(4'b0000), .out(multiplexer_47_out), .sel(comparator_49_eq));
  Comparator #(.width(7)) comparator_50 (.a(7'b0100011), .b(Instruction[6:0]), .eq(comparator_50_eq));  // open: gt, lt
  Multiplexer #(.width(4)) multiplexer_48 (
    .in0(4'b0000), .in1(4'b0000), .out(multiplexer_48_out), .sel(comparator_50_eq));
  Comparator #(.width(7)) comparator_51 (.a(7'b0110111), .b(Instruction[6:0]), .eq(comparator_51_eq));  // open: gt, lt
  Multiplexer #(.width(4)) multiplexer_49 (
    .in0(4'b0000), .in1(4'b1111), .out(multiplexer_49_out), .sel(comparator_51_eq));
  Comparator #(.width(7)) comparator_52 (.a(7'b0010111), .b(Instruction[6:0]), .eq(comparator_52_eq));  // open: gt, lt
  Multiplexer #(.width(4)) multiplexer_50 (
    .in0(4'b0000), .in1(4'b0000), .out(multiplexer_50_out), .sel(comparator_52_eq));
  Comparator #(.width(7)) comparator_53 (.a(7'b1101111), .b(Instruction[6:0]), .eq(comparator_53_eq));  // open: gt, lt
  Multiplexer #(.width(4)) multiplexer_51 (
    .in0(4'b0000), .in1(4'b0000), .out(multiplexer_51_out), .sel(comparator_53_eq));
  Comparator #(.width(7)) comparator_54 (.a(7'b1100111), .b(Instruction[6:0]), .eq(comparator_54_eq));  // open: gt, lt
  Multiplexer #(.width(4)) multiplexer_52 (
    .in0(4'b0000), .in1(4'b0000), .out(multiplexer_52_out), .sel(comparator_54_eq));
  Multiplexer #(.width(4)) multiplexer_53 (
    .in0(multiplexer_42_out), .in1(4'b1101), .out(multiplexer_53_out), .sel(comparator_55_eq));
  Comparator #(.width(7)) comparator_55 (
    .a(7'b0100000), .b(Instruction[31:25]), .eq(comparator_55_eq));  // open: gt, lt
  Multiplexer #(.width(4)) multiplexer_54 (
    .in0(multiplexer_43_out), .in1(4'b1100), .out(multiplexer_54_out), .sel(comparator_56_eq));
  Comparator #(.width(7)) comparator_56 (
    .a(7'b0100000), .b(Instruction[31:25]), .eq(comparator_56_eq));  // open: gt, lt
  Multiplexer #(.width(4)) multiplexer_55 (
    .in0(multiplexer_44_out), .in1(4'b1001), .out(multiplexer_55_out), .sel(comparator_57_eq));
  Comparator #(.width(7)) comparator_57 (
    .a(7'b0000001), .b(Instruction[31:25]), .eq(comparator_57_eq));  // open: gt, lt
  Multiplexer #(.width(4)) multiplexer_56 (
    .in0(multiplexer_45_out), .in1(4'b1101), .out(multiplexer_56_out), .sel(comparator_58_eq));
  Comparator #(.width(7)) comparator_58 (
    .a(7'b0100000), .b(Instruction[31:25]), .eq(comparator_58_eq));  // open: gt, lt
  or or_4 (ASel, multiplexer_30_out, multiplexer_31_out, multiplexer_32_out);
  or or_5 (BSel, multiplexer_33_out, multiplexer_34_out, multiplexer_35_out, multiplexer_36_out, multiplexer_37_out, multiplexer_38_out, multiplexer_39_out, multiplexer_40_out, multiplexer_41_out);
  Multiplexer #(.select(3), .width(4)) multiplexer_57 (
    .in0(4'b0000), .in1(4'b0001), .in2(4'b0010), .in4(4'b0100), .in5(multiplexer_53_out), .in6(4'b0110),
    .in7(4'b0111), .out(multiplexer_57_out), .sel(Instruction[14:12]));  // open: in3
  Multiplexer #(.width(4)) multiplexer_58 (
    .in0(multiplexer_54_out), .in1(4'b1000), .out(multiplexer_58_out), .sel(comparator_59_eq));
  Comparator #(.width(7)) comparator_59 (
    .a(7'b0000001), .b(Instruction[31:25]), .eq(comparator_59_eq));  // open: gt, lt
  Multiplexer #(.width(4)) multiplexer_59 (
    .in0(4'b0000), .in1(multiplexer_57_out), .out(multiplexer_59_out), .sel(comparator_43_eq));
  Multiplexer #(.width(4)) multiplexer_60 (
    .in0(4'b0000), .in1(multiplexer_61_out), .out(multiplexer_60_out), .sel(comparator_44_eq));
  Multiplexer #(.select(3), .width(4)) multiplexer_61 (
    .in0(multiplexer_58_out), .in1(multiplexer_55_out), .in2(4'b0010), .in3(4'b1011), .in4(4'b0100),
    .in5(multiplexer_56_out), .in6(4'b0110), .in7(4'b0111), .out(multiplexer_61_out), .sel(Instruction[14:12]));
  assign ALUSel = multiplexer_59_out | multiplexer_60_out | multiplexer_46_out | multiplexer_47_out | multiplexer_48_out | multiplexer_49_out | multiplexer_50_out | multiplexer_51_out | multiplexer_52_out;  // OR_Gate or_6, 4 bits wide
  Comparator #(.width(7)) comparator_60 (.a(7'b0100011), .b(Instruction[6:0]), .eq(comparator_60_eq));  // open: gt, lt
  Comparator #(.width(7)) comparator_61 (.a(7'b0000011), .b(Instruction[6:0]), .eq(comparator_61_eq));  // open: gt, lt
  Multiplexer #(.width(2)) multiplexer_62 (.in0(2'b00), .in1(2'b00), .out(multiplexer_62_out), .sel(comparator_61_eq));
  Comparator #(.width(7)) comparator_62 (.a(7'b1101111), .b(Instruction[6:0]), .eq(comparator_62_eq));  // open: gt, lt
  Multiplexer #(.width(2)) multiplexer_63 (.in0(2'b00), .in1(2'b10), .out(multiplexer_63_out), .sel(comparator_62_eq));
  Comparator #(.width(7)) comparator_63 (.a(7'b1100111), .b(Instruction[6:0]), .eq(comparator_63_eq));  // open: gt, lt
  Multiplexer #(.width(2)) multiplexer_64 (.in0(2'b00), .in1(2'b10), .out(multiplexer_64_out), .sel(comparator_63_eq));
  Multiplexer multiplexer_65 (.in0(1'b0), .in1(1'b1), .out(MemRW), .sel(comparator_60_eq));
  assign or_7_out = multiplexer_62_out | multiplexer_63_out | multiplexer_64_out;  // OR_Gate or_7, 2 bits wide
  Comparator #(.width(2)) comparator_64 (.a(2'b00), .b(or_7_out), .eq(comparator_64_eq));  // open: gt, lt
  not not_4 (not_4_out, comparator_61_eq);
  and and_1 (and_1_out, not_4_out, comparator_64_eq);
  Multiplexer #(.width(2)) multiplexer_66 (.in0(or_7_out), .in1(2'b01), .out(WBSel), .sel(and_1_out));

  // Notes on the sheet:
  //   INPUTS to your circuit
  //   beq
  //   jal
  //   jalr, I-format
  //   I-type Instruction
  //   B-type Instruction
  //   L-type Instruction, I-format
  //   S-type Instruction
  //   lui
  //   auipc
  //   jal
  //   jalr, I-format
  //   I-type Instruction
  //   R-type Instruction
  //   B-type Instruction
  //   L-type Instruction
  //   S-type Instruction
  //   lui
  //   auipc
  //   jal
  //   jalr, I-format
  //   Connect ROM Input here ->
  //   PCSel Control
  //   B-type Instruction
  //   Function 3
  //   bge
  //   ImmSel Control
  //   RegWEn Control
  //   BrUn Control
  //   B-type Instruction
  //   bgeu
  //   Function 3
  //   ROM FOR CONTROL LOGIC
  //   blt
  //   bltu
  //   bne
  //   DON'T CHANGE THE LOCATIONS OF THE INPUTS AND OUTPUTS!
  //   This is only if you choose to do the ROM option
  //   CONNECT
  //   WIRE
  //   TO
  //   USE
  //   ROM
  //   OUTPUT from your circuit
  //   B-type Instruction
  //   auipc
  //   jal
  //   I-type Instruction
  //   R-type Instruction
  //   B-type Instruction
  //   L-type Instruction
  //   S-type Instruction
  //   lui
  //   auipc
  //   jal
  //   jalr, I-format
  //   I-type Instruction
  //   R-type Instruction
  //   B-type Instruction
  //   L-type Instruction
  //   S-type Instruction
  //   lui
  //   auipc
  //   jal
  //   jalr, I-format
  //   Reminder: If using ROM, use combinational logic for PCSel
  //   ASel Control
  //   BSel Control
  //   ALU Select Control
  //   Function 7
  //   Function 3
  //   L-type Instruction
  //   MemRW Control
  //   S-type Instruction
  //   WBSel Control
  //   jal
  //   jalr, I-format
endmodule
