// Logisim project regfile.circ as structural Verilog: 1 circuit, main circuit regfile
module regfile (
  input  [4:0] ReadIndex1,
  input  [4:0] ReadIndex2,
  input  [4:0] WriteIndex,
  input  [31:0] WriteData,
  input  RegWEn,
  input  clk,
  output [31:0] ra,
  output [31:0] sp,
  output [31:0] t0,
  output [31:0] t1,
  output [31:0] t2,
  output [31:0] s0,
  output [31:0] s1,
  output [31:0] a0,
  output [31:0] ReadData1,
  output [31:0] ReadData2
);

  wire and_1_out, and_2_out, and_3_out, and_4_out, and_5_out, and_6_out, and_7_out, and_8_out, and_9_out,
       and_10_out, and_11_out, and_12_out, and_13_out, and_14_out, and_15_out, and_16_out, and_17_out,
       and_18_out, and_19_out, and_20_out, and_21_out, and_22_out, and_23_out, and_24_out, and_25_out,
       and_26_out, and_27_out, and_28_out, and_29_out, and_30_out, and_31_out, w1, w2, w3, w4, w5, w6, w7,
       w8, w9, w10, w11, w12, w13, w14, w15, w16, w17, w18, w19, w20, w21, w22, w23, w24, w25, w26, w27, w28,
       w29, w30, w31;
  wire [31:0] r3, r4, r11, r12, r13, r14, r15, r16, r17, r18, r19, r20, r21, r22, r23, r24, r25, r26, r27,
       r28, r29, r30, r31;

  Demultiplexer #(.select(5)) demultiplexer_1 (
    .out1(w1), .out2(w2), .out3(w3), .out4(w4), .out5(w5), .out6(w6), .out7(w7), .out8(w8), .out9(w9),
    .out10(w10), .out11(w11), .out12(w12), .out13(w13), .out14(w14), .out15(w15), .out16(w16), .out17(w17),
    .out18(w18), .out19(w19), .out20(w20), .out21(w21), .out22(w22), .out23(w23), .out24(w24), .out25(w25),
    .out26(w26), .out27(w27), .out28(w28), .out29(w29), .out30(w30), .out31(w31), .in(1'b1), .sel(WriteIndex));  // open: out0
  Register #(.width(32)) register_1 (.D(WriteData), .en(and_1_out), .clk(clk), .Q(r4));  // open: clr
  and and_1 (and_1_out, w4, RegWEn);
  Register #(.width(32)) register_2 (.D(WriteData), .en(and_2_out), .clk(clk), .Q(s0));  // open: clr
  and and_2 (and_2_out, w8, RegWEn);
  Register #(.width(32)) register_3 (.D(WriteData), .en(and_3_out), .clk(clk), .Q(r12));  // open: clr
  and and_3 (and_3_out, w12, RegWEn);
  Register #(.width(32)) register_4 (.D(WriteData), .en(and_4_out), .clk(clk), .Q(r16));  // open: clr
  and and_4 (and_4_out, w16, RegWEn);
  Register #(.width(32)) register_5 (.D(WriteData), .en(and_5_out), .clk(clk), .Q(r20));  // open: clr
  and and_5 (and_5_out, w20, RegWEn);
  Register #(.width(32)) register_6 (.D(WriteData), .en(and_6_out), .clk(clk), .Q(r24));  // open: clr
  and and_6 (and_6_out, w24, RegWEn);
  Register #(.width(32)) register_7 (.D(WriteData), .en(and_7_out), .clk(clk), .Q(r28));  // open: clr
  and and_7 (and_7_out, w28, RegWEn);
  and and_8 (and_8_out, w1, RegWEn);
  and and_9 (and_9_out, w5, RegWEn);
  and and_10 (and_10_out, w9, RegWEn);
  and and_11 (and_11_out, w13, RegWEn);
  and and_12 (and_12_out, w17, RegWEn);
  and and_13 (and_13_out, w21, RegWEn);
  and and_14 (and_14_out, w25, RegWEn);
  and and_15 (and_15_out, w29, RegWEn);
  Register #(.width(32)) x1 (.D(WriteData), .en(and_8_out), .clk(clk), .Q(ra));  // open: clr
  Register #(.width(32)) register_8 (.D(WriteData), .en(and_9_out), .clk(clk), .Q(t0));  // open: clr
  Register #(.width(32)) register_9 (.D(WriteData), .en(and_10_out), .clk(clk), .Q(s1));  // open: clr
  Register #(.width(32)) register_10 (.D(WriteData), .en(and_11_out), .clk(clk), .Q(r13));  // open: clr
  Register #(.width(32)) register_11 (.D(WriteData), .en(and_12_out), .clk(clk), .Q(r17));  // open: clr
  Register #(.width(32)) register_12 (.D(WriteData), .en(and_13_out), .clk(clk), .Q(r21));  // open: clr
  Register #(.width(32)) register_13 (.D(WriteData), .en(and_14_out), .clk(clk), .Q(r25));  // open: clr
  Register #(.width(32)) register_14 (.D(WriteData), .en(and_15_out), .clk(clk), .Q(r29));  // open: clr
  Register #(.width(32)) x2 (.D(WriteData), .en(and_16_out), .clk(clk), .Q(sp));  // open: clr
  and and_16 (and_16_out, w2, RegWEn);
  Register #(.width(32)) register_15 (.D(WriteData), .en(and_17_out), .clk(clk), .Q(t1));  // open: clr
  and and_17 (and_17_out, w6, RegWEn);
  Register #(.width(32)) register_16 (.D(WriteData), .en(and_18_out), .clk(clk), .Q(a0));  // open: clr
  and and_18 (and_18_out, w10, RegWEn);
  Register #(.width(32)) register_17 (.D(WriteData), .en(and_19_out), .clk(clk), .Q(r14));  // open: clr
  and and_19 (and_19_out, w14, RegWEn);
  Register #(.width(32)) register_18 (.D(WriteData), .en(and_20_out), .clk(clk), .Q(r18));  // open: clr
  and and_20 (and_20_out, w18, RegWEn);
  Register #(.width(32)) register_19 (.D(WriteData), .en(and_21_out), .clk(clk), .Q(r22));  // open: clr
  and and_21 (and_21_out, w22, RegWEn);
  Register #(.width(32)) register_20 (.D(WriteData), .en(and_22_out), .clk(clk), .Q(r26));  // open: clr
  and and_22 (and_22_out, w26, RegWEn);
  Register #(.width(32)) register_21 (.D(WriteData), .en(and_23_out), .clk(clk), .Q(r30));  // open: clr
  and and_23 (and_23_out, w30, RegWEn);
  Register #(.width(32)) x3 (.D(WriteData), .en(and_24_out), .clk(clk), .Q(r3));  // open: clr
  and and_24 (and_24_out, w3, RegWEn);
  Register #(.width(32)) register_22 (.D(WriteData), .en(and_25_out), .clk(clk), .Q(t2));  // open: clr
  and and_25 (and_25_out, w7, RegWEn);
  Register #(.width(32)) register_23 (.D(WriteData), .en(and_26_out), .clk(clk), .Q(r11));  // open: clr
  and and_26 (and_26_out, w11, RegWEn);
  Register #(.width(32)) register_24 (.D(WriteData), .en(and_27_out), .clk(clk), .Q(r15));  // open: clr
  and and_27 (and_27_out, w15, RegWEn);
  Register #(.width(32)) register_25 (.D(WriteData), .en(and_28_out), .clk(clk), .Q(r19));  // open: clr
  and and_28 (and_28_out, w19, RegWEn);
  Register #(.width(32)) register_26 (.D(WriteData), .en(and_29_out), .clk(clk), .Q(r23));  // open: clr
  and and_29 (and_29_out, w23, RegWEn);
  Register #(.width(32)) register_27 (.D(WriteData), .en(and_30_out), .clk(clk), .Q(r27));  // open: clr
  and and_30 (and_30_out, w27, RegWEn);
  Register #(.width(32)) register_28 (.D(WriteData), .en(and_31_out), .clk(clk), .Q(r31));  // open: clr
  and and_31 (and_31_out, w31, RegWEn);
  Multiplexer #(.select(5), .width(32)) multiplexer_1 (
    .in0({32{1'b0}}), .in1(ra), .in2(sp), .in3(r3), .in4(r4), .in5(t0), .in6(t1), .in7(t2), .in8(s0),
    .in9(s1), .in10(a0), .in11(r11), .in12(r12), .in13(r13), .in14(r14), .in15(r15), .in16(r16), .in17(r17),
    .in18(r18), .in19(r19), .in20(r20), .in21(r21), .in22(r22), .in23(r23), .in24(r24), .in25(r25),
    .in26(r26), .in27(r27), .in28(r28), .in29(r29), .in30(r30), .in31(r31), .out(ReadData1), .sel(ReadIndex1));
  Multiplexer #(.select(5), .width(32)) multiplexer_2 (
    .in0({32{1'b0}}), .in1(ra), .in2(sp), .in3(r3), .in4(r4), .in5(t0), .in6(t1), .in7(t2), .in8(s0),
    .in9(s1), .in10(a0), .in11(r11), .in12(r12), .in13(r13), .in14(r14), .in15(r15), .in16(r16), .in17(r17),
    .in18(r18), .in19(r19), .in20(r20), .in21(r21), .in22(r22), .in23(r23), .in24(r24), .in25(r25),
    .in26(r26), .in27(r27), .in28(r28), .in29(r29), .in30(r30), .in31(r31), .out(ReadData2), .sel(ReadIndex2));

  // Other names for the same wires on the sheet: r1[31:0] = ra; r2[31:0] = sp; r5[31:0] = t0; r6[31:0] = t1;
  //   r7[31:0] = t2; r8[31:0] = s0; r9[31:0] = s1; r10[31:0] = a0

  // Notes on the sheet:
  //   INPUTS to your circuit
  //   DON'T CHANGE THE LOCATIONS OF THE INPUTS AND OUTPUTS!
  //   These are DEBUG/TEST outputs from your circuit.
  //   OUTPUTS from your circuit
endmodule
